// Logisim project lab12.circ as structural Verilog: 5 circuits, main circuit main
module main (
  input  in_1,
  input  [4:0] in_2,
  input  [4:0] in_3,
  input  [4:0] in_4,
  input  [31:0] in_5,
  output [31:0] out_6,
  output [31:0] out_7
);

  RegisterFile registerfile_1 (
    .write(in_1), .regnum(in_2), .reg1(in_3), .reg2(in_4), .dataWrite(in_5), .data1(out_6), .data2(out_7));
endmodule

module Dlatch (
  input  C,
  input  D,
  output Q,
  output Q1
);

  wire and_1_out, and_2_out, not_1_out, or_1_out, or_2_out;

  not not_1 (not_1_out, D);
  and and_1 (and_1_out, C, not_1_out);
  and and_2 (and_2_out, C, D);
  or or_1 (or_1_out, and_1_out, Q1);
  not not_2 (Q, or_1_out);
  or or_2 (or_2_out, Q, and_2_out);
  not not_3 (Q1, or_2_out);
endmodule

module DFlipFlop (
  input  D,
  input  C,
  output Q,
  output Q1
);

  wire dlatch_1_q, not_1_out;

  Dlatch dlatch_1 (.C(C), .D(D), .Q(dlatch_1_q));  // open: Q1
  not not_1 (not_1_out, C);
  Dlatch dlatch_2 (.C(not_1_out), .D(dlatch_1_q), .Q(Q), .Q1(Q1));
endmodule

module Registerr (
  input  clock,
  input  [31:0] in_2,
  output [31:0] out_3
);

  DFlipFlop dflipflop_1 (.D(in_2[0]), .C(clock), .Q(out_3[0]));  // open: Q1
  DFlipFlop dflipflop_2 (.D(in_2[1]), .C(clock), .Q(out_3[1]));  // open: Q1
  DFlipFlop dflipflop_3 (.D(in_2[2]), .C(clock), .Q(out_3[2]));  // open: Q1
  DFlipFlop dflipflop_4 (.D(in_2[3]), .C(clock), .Q(out_3[3]));  // open: Q1
  DFlipFlop dflipflop_5 (.D(in_2[4]), .C(clock), .Q(out_3[4]));  // open: Q1
  DFlipFlop dflipflop_6 (.D(in_2[5]), .C(clock), .Q(out_3[5]));  // open: Q1
  DFlipFlop dflipflop_7 (.D(in_2[6]), .C(clock), .Q(out_3[6]));  // open: Q1
  DFlipFlop dflipflop_8 (.D(in_2[7]), .C(clock), .Q(out_3[7]));  // open: Q1
  DFlipFlop dflipflop_9 (.D(in_2[8]), .C(clock), .Q(out_3[8]));  // open: Q1
  DFlipFlop dflipflop_10 (.D(in_2[9]), .C(clock), .Q(out_3[9]));  // open: Q1
  DFlipFlop dflipflop_11 (.D(in_2[10]), .C(clock), .Q(out_3[10]));  // open: Q1
  DFlipFlop dflipflop_12 (.D(in_2[11]), .C(clock), .Q(out_3[11]));  // open: Q1
  DFlipFlop dflipflop_13 (.D(in_2[12]), .C(clock), .Q(out_3[12]));  // open: Q1
  DFlipFlop dflipflop_14 (.D(in_2[13]), .C(clock), .Q(out_3[13]));  // open: Q1
  DFlipFlop dflipflop_15 (.D(in_2[14]), .C(clock), .Q(out_3[14]));  // open: Q1
  DFlipFlop dflipflop_16 (.D(in_2[15]), .C(clock), .Q(out_3[15]));  // open: Q1
  DFlipFlop dflipflop_17 (.D(in_2[16]), .C(clock), .Q(out_3[16]));  // open: Q1
  DFlipFlop dflipflop_18 (.D(in_2[17]), .C(clock), .Q(out_3[17]));  // open: Q1
  DFlipFlop dflipflop_19 (.D(in_2[18]), .C(clock), .Q(out_3[18]));  // open: Q1
  DFlipFlop dflipflop_20 (.D(in_2[19]), .C(clock), .Q(out_3[19]));  // open: Q1
  DFlipFlop dflipflop_21 (.D(in_2[20]), .C(clock), .Q(out_3[20]));  // open: Q1
  DFlipFlop dflipflop_22 (.D(in_2[21]), .C(clock), .Q(out_3[21]));  // open: Q1
  DFlipFlop dflipflop_23 (.D(in_2[22]), .C(clock), .Q(out_3[22]));  // open: Q1
  DFlipFlop dflipflop_24 (.D(in_2[23]), .C(clock), .Q(out_3[23]));  // open: Q1
  DFlipFlop dflipflop_25 (.D(in_2[24]), .C(clock), .Q(out_3[24]));  // open: Q1
  DFlipFlop dflipflop_26 (.D(in_2[25]), .C(clock), .Q(out_3[25]));  // open: Q1
  DFlipFlop dflipflop_27 (.D(in_2[26]), .C(clock), .Q(out_3[26]));  // open: Q1
  DFlipFlop dflipflop_28 (.D(in_2[27]), .C(clock), .Q(out_3[27]));  // open: Q1
  DFlipFlop dflipflop_29 (.D(in_2[28]), .C(clock), .Q(out_3[28]));  // open: Q1
  DFlipFlop dflipflop_30 (.D(in_2[29]), .C(clock), .Q(out_3[29]));  // open: Q1
  DFlipFlop dflipflop_31 (.D(in_2[30]), .C(clock), .Q(out_3[30]));  // open: Q1
  DFlipFlop dflipflop_32 (.D(in_2[31]), .C(clock), .Q(out_3[31]));  // open: Q1
endmodule

module RegisterFile (
  input  write,
  input  [4:0] regnum,
  input  [4:0] reg1,
  input  [4:0] reg2,
  input  [31:0] dataWrite,
  output [31:0] data1,
  output [31:0] data2
);

  wire and_1_out, and_2_out, and_3_out, and_4_out, and_5_out, and_6_out, and_7_out, and_8_out, and_9_out,
       and_10_out, and_11_out, and_12_out, and_13_out, and_14_out, and_15_out, and_16_out, and_17_out,
       and_18_out, and_19_out, and_20_out, and_21_out, and_22_out, and_23_out, and_24_out, and_25_out,
       and_26_out, and_27_out, and_28_out, and_29_out, and_30_out, and_31_out, and_32_out, decoder_1_out0,
       decoder_1_out1, decoder_1_out2, decoder_1_out3, decoder_1_out4, decoder_1_out5, decoder_1_out6,
       decoder_1_out7, decoder_1_out8, decoder_1_out9, decoder_1_out10, decoder_1_out11, decoder_1_out12,
       decoder_1_out13, decoder_1_out14, decoder_1_out15, decoder_1_out16, decoder_1_out17, decoder_1_out18,
       decoder_1_out19, decoder_1_out20, decoder_1_out21, decoder_1_out22, decoder_1_out23, decoder_1_out24,
       decoder_1_out25, decoder_1_out26, decoder_1_out27, decoder_1_out28, decoder_1_out29, decoder_1_out30,
       decoder_1_out31;
  wire [31:0] registerr_1_out_3, registerr_2_out_3, registerr_3_out_3, registerr_4_out_3, registerr_5_out_3,
       registerr_6_out_3, registerr_7_out_3, registerr_8_out_3, registerr_9_out_3, registerr_10_out_3,
       registerr_11_out_3, registerr_12_out_3, registerr_13_out_3, registerr_14_out_3, registerr_15_out_3,
       registerr_16_out_3, registerr_17_out_3, registerr_18_out_3, registerr_19_out_3, registerr_20_out_3,
       registerr_21_out_3, registerr_22_out_3, registerr_23_out_3, registerr_24_out_3, registerr_25_out_3,
       registerr_26_out_3, registerr_27_out_3, registerr_28_out_3, registerr_29_out_3, registerr_30_out_3,
       registerr_31_out_3, registerr_32_out_3;

  Decoder #(.enable("false"), .select(5)) decoder_1 (
    .out0(decoder_1_out0), .out1(decoder_1_out1), .out2(decoder_1_out2), .out3(decoder_1_out3),
    .out4(decoder_1_out4), .out5(decoder_1_out5), .out6(decoder_1_out6), .out7(decoder_1_out7),
    .out8(decoder_1_out8), .out9(decoder_1_out9), .out10(decoder_1_out10), .out11(decoder_1_out11),
    .out12(decoder_1_out12), .out13(decoder_1_out13), .out14(decoder_1_out14), .out15(decoder_1_out15),
    .out16(decoder_1_out16), .out17(decoder_1_out17), .out18(decoder_1_out18), .out19(decoder_1_out19),
    .out20(decoder_1_out20), .out21(decoder_1_out21), .out22(decoder_1_out22), .out23(decoder_1_out23),
    .out24(decoder_1_out24), .out25(decoder_1_out25), .out26(decoder_1_out26), .out27(decoder_1_out27),
    .out28(decoder_1_out28), .out29(decoder_1_out29), .out30(decoder_1_out30), .out31(decoder_1_out31),
    .sel(regnum));
  and and_1 (and_1_out, decoder_1_out0, write);
  and and_2 (and_2_out, decoder_1_out1, write);
  and and_3 (and_3_out, decoder_1_out2, write);
  and and_4 (and_4_out, decoder_1_out3, write);
  and and_5 (and_5_out, decoder_1_out4, write);
  and and_6 (and_6_out, decoder_1_out5, write);
  and and_7 (and_7_out, decoder_1_out6, write);
  and and_8 (and_8_out, decoder_1_out7, write);
  and and_9 (and_9_out, decoder_1_out8, write);
  and and_10 (and_10_out, decoder_1_out9, write);
  and and_11 (and_11_out, decoder_1_out10, write);
  and and_12 (and_12_out, decoder_1_out11, write);
  and and_13 (and_13_out, decoder_1_out12, write);
  and and_14 (and_14_out, decoder_1_out13, write);
  and and_15 (and_15_out, decoder_1_out14, write);
  and and_16 (and_16_out, decoder_1_out15, write);
  and and_17 (and_17_out, decoder_1_out16, write);
  and and_18 (and_18_out, decoder_1_out17, write);
  and and_19 (and_19_out, decoder_1_out18, write);
  and and_20 (and_20_out, decoder_1_out19, write);
  and and_21 (and_21_out, decoder_1_out20, write);
  and and_22 (and_22_out, decoder_1_out21, write);
  and and_23 (and_23_out, decoder_1_out22, write);
  and and_24 (and_24_out, decoder_1_out23, write);
  and and_25 (and_25_out, decoder_1_out24, write);
  and and_26 (and_26_out, decoder_1_out25, write);
  and and_27 (and_27_out, decoder_1_out26, write);
  and and_28 (and_28_out, decoder_1_out27, write);
  and and_29 (and_29_out, decoder_1_out28, write);
  and and_30 (and_30_out, decoder_1_out29, write);
  and and_31 (and_31_out, decoder_1_out30, write);
  and and_32 (and_32_out, decoder_1_out31, write);
  Registerr registerr_1 (.clock(and_1_out), .in_2(dataWrite), .out_3(registerr_1_out_3));
  Registerr registerr_2 (.clock(and_2_out), .in_2(dataWrite), .out_3(registerr_2_out_3));
  Registerr registerr_3 (.clock(and_3_out), .in_2(dataWrite), .out_3(registerr_3_out_3));
  Registerr registerr_4 (.clock(and_4_out), .in_2(dataWrite), .out_3(registerr_4_out_3));
  Registerr registerr_5 (.clock(and_5_out), .in_2(dataWrite), .out_3(registerr_5_out_3));
  Registerr registerr_6 (.clock(and_6_out), .in_2(dataWrite), .out_3(registerr_6_out_3));
  Registerr registerr_7 (.clock(and_7_out), .in_2(dataWrite), .out_3(registerr_7_out_3));
  Registerr registerr_8 (.clock(and_8_out), .in_2(dataWrite), .out_3(registerr_8_out_3));
  Registerr registerr_9 (.clock(and_9_out), .in_2(dataWrite), .out_3(registerr_9_out_3));
  Registerr registerr_10 (.clock(and_10_out), .in_2(dataWrite), .out_3(registerr_10_out_3));
  Registerr registerr_11 (.clock(and_11_out), .in_2(dataWrite), .out_3(registerr_11_out_3));
  Registerr registerr_12 (.clock(and_12_out), .in_2(dataWrite), .out_3(registerr_12_out_3));
  Registerr registerr_13 (.clock(and_13_out), .in_2(dataWrite), .out_3(registerr_13_out_3));
  Registerr registerr_14 (.clock(and_14_out), .in_2(dataWrite), .out_3(registerr_14_out_3));
  Registerr registerr_15 (.clock(and_15_out), .in_2(dataWrite), .out_3(registerr_15_out_3));
  Registerr registerr_16 (.clock(and_16_out), .in_2(dataWrite), .out_3(registerr_16_out_3));
  Registerr registerr_17 (.clock(and_17_out), .in_2(dataWrite), .out_3(registerr_17_out_3));
  Registerr registerr_18 (.clock(and_18_out), .in_2(dataWrite), .out_3(registerr_18_out_3));
  Registerr registerr_19 (.clock(and_19_out), .in_2(dataWrite), .out_3(registerr_19_out_3));
  Registerr registerr_20 (.clock(and_20_out), .in_2(dataWrite), .out_3(registerr_20_out_3));
  Registerr registerr_21 (.clock(and_21_out), .in_2(dataWrite), .out_3(registerr_21_out_3));
  Registerr registerr_22 (.clock(and_22_out), .in_2(dataWrite), .out_3(registerr_22_out_3));
  Registerr registerr_23 (.clock(and_23_out), .in_2(dataWrite), .out_3(registerr_23_out_3));
  Registerr registerr_24 (.clock(and_24_out), .in_2(dataWrite), .out_3(registerr_24_out_3));
  Registerr registerr_25 (.clock(and_25_out), .in_2(dataWrite), .out_3(registerr_25_out_3));
  Registerr registerr_26 (.clock(and_26_out), .in_2(dataWrite), .out_3(registerr_26_out_3));
  Registerr registerr_27 (.clock(and_27_out), .in_2(dataWrite), .out_3(registerr_27_out_3));
  Registerr registerr_28 (.clock(and_28_out), .in_2(dataWrite), .out_3(registerr_28_out_3));
  Registerr registerr_29 (.clock(and_29_out), .in_2(dataWrite), .out_3(registerr_29_out_3));
  Registerr registerr_30 (.clock(and_30_out), .in_2(dataWrite), .out_3(registerr_30_out_3));
  Registerr registerr_31 (.clock(and_31_out), .in_2(dataWrite), .out_3(registerr_31_out_3));
  Registerr registerr_32 (.clock(and_32_out), .in_2(dataWrite), .out_3(registerr_32_out_3));
  Multiplexer #(.select(5), .width(32)) multiplexer_1 (
    .in0(registerr_1_out_3), .in1(registerr_2_out_3), .in2(registerr_3_out_3), .in3(registerr_4_out_3),
    .in4(registerr_5_out_3), .in5(registerr_6_out_3), .in6(registerr_7_out_3), .in7(registerr_8_out_3),
    .in8(registerr_9_out_3), .in9(registerr_10_out_3), .in10(registerr_11_out_3), .in11(registerr_12_out_3),
    .in12(registerr_13_out_3), .in13(registerr_14_out_3), .in14(registerr_15_out_3),
    .in15(registerr_16_out_3), .in16(registerr_17_out_3), .in17(registerr_18_out_3),
    .in18(registerr_19_out_3), .in19(registerr_20_out_3), .in20(registerr_21_out_3),
    .in21(registerr_22_out_3), .in22(registerr_23_out_3), .in23(registerr_24_out_3),
    .in24(registerr_25_out_3), .in25(registerr_26_out_3), .in26(registerr_27_out_3),
    .in27(registerr_28_out_3), .in28(registerr_29_out_3), .in29(registerr_30_out_3),
    .in30(registerr_31_out_3), .in31(registerr_32_out_3), .out(data1), .sel(reg1));
  Multiplexer #(.select(5), .width(32)) multiplexer_2 (
    .in0(registerr_1_out_3), .in1(registerr_2_out_3), .in2(registerr_3_out_3), .in3(registerr_4_out_3),
    .in4(registerr_5_out_3), .in5(registerr_6_out_3), .in6(registerr_7_out_3), .in7(registerr_8_out_3),
    .in8(registerr_9_out_3), .in9(registerr_10_out_3), .in10(registerr_11_out_3), .in11(registerr_12_out_3),
    .in12(registerr_13_out_3), .in13(registerr_14_out_3), .in14(registerr_15_out_3),
    .in15(registerr_16_out_3), .in16(registerr_17_out_3), .in17(registerr_18_out_3),
    .in18(registerr_19_out_3), .in19(registerr_20_out_3), .in20(registerr_21_out_3),
    .in21(registerr_22_out_3), .in22(registerr_23_out_3), .in23(registerr_24_out_3),
    .in24(registerr_25_out_3), .in25(registerr_26_out_3), .in26(registerr_27_out_3),
    .in27(registerr_28_out_3), .in28(registerr_29_out_3), .in29(registerr_30_out_3),
    .in30(registerr_31_out_3), .in31(registerr_32_out_3), .out(data2), .sel(reg2));
endmodule
